# Fritzing sketch SODONGUYENLT (saved by Fritzing 0.9.3b)
circuit board: 7.11601cm x 7.34132cm

parts:
  DHT1 = DHT11 Humitidy and Temperature Sensor
  Power_plug1 = Power plug
  U2 = ESP32S-HiLetgo [part_number=ESP32S-HiLetgo]
  R1 = Resistor [tolerance=±5% resistance=220 package="2512 [SMD]"]
  R2 = Resistor [tolerance=±5% resistance=220 package="2512 [SMD]"]
  R3 = Resistor [tolerance=±5% resistance=220 package="2512 [SMD]"]
  M3 = DC Motor
  LED4 = LEDs [package=led10mm]
  Part1 = MQ-3 breakout
  LED6 = LEDs [package=led10mm]
  LED7 = LEDs [package=led10mm]
  KY-8 = Keyes Relay [package=THT]
  KY-6 = Keyes Relay [package=THT]
  KY-9 = Keyes Relay [package=THT]
  KY-5 = Keyes Relay [package=THT]

nets (from the breadboard view):
  VDD: DHT1.VDD, U2.VIN, Part1.VCC, KY-6.power, KY-5.power
  N1: DHT1.DATA, U2.GPIO2
  GND: DHT1.GND, U2.GND, Part1.GND, KY-8.ground, KY-6.ground, KY-9.ground
  N2: Power_plug1.GND, KY-8.C
  N3: Power_plug1.VCC, M3.pin_1, LED4.C, LED6.C, LED7.C
  N4: U2.GPIO34, Part1.AO
  N5: U2.GPIO4, KY-8.signal
  N6: U2.GPIO5, KY-9.signal
  N7: U2.GPIO18, KY-6.signal
  N8: U2.GPIO19, KY-5.signal
  N9: R1.Pin_0, LED6.A
  N10: R1.Pin_1, KY-9.NO
  N11: R2.Pin_0, LED7.A
  N12: R2.Pin_1, KY-6.NO
  N13: R3.Pin_0, LED4.A
  N14: R3.Pin_1, KY-5.NO
  N15: M3.pin_2, KY-8.NO

notes:
  5VDC

custom parts:
  DHT11 Humitidy and Temperature Sensor: DHT11 Humidity and Temperature Sensor
  ESP32S-HiLetgo: HiLetgo ESP-WROOM-32 ESP32 ESP-32S Development Board 2.4GHz Dual-Mode WiFi + Bluetooth Dual Cores Microcontroller The ESP32 integrated with Antenna switches, RF Balun, power amplifiers, low-noise amplifiers, filters, and management modules, and the entire solution occupies the least area of PCB. 2.4 GHz Wi-Fi plus Bluetooth dual-mode chip, with TSMC Ultra-low power consumption 40nm technology,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
  MQ-3 breakout: Alcohol sensor is capable of detecting alcohol (ethanol) particles on itself and gives the information in digital form back to us to manipulate with it. SKU:101251 • Voltage: 5V DC • Power: max 750mW • Measurement range: 0.04-4mg/L
  Keyes Relay: The Keyes 5V relay module is suitable for SCM development, home appliance control. It uses a 5V~12V TIL control signal which can control DC / AC signal.
